# Fritzing sketch thermoControl (saved by Fritzing 0.9.10b)
breadboards: 2

parts:
  S1 = Pushbutton [package="[THT]"]
  S2 = Pushbutton [package="[THT]"]
  S3 = Pushbutton [package="[THT]"]
  LED1 = LED - 5mm [color="Red (633nm)" current=0.030 package="5 mm [THT]"]
  LED2 = LED - 5mm [color="Blue (525nm)" current=0.030 package="5 mm [THT]"]
  R1 = Resistor [tolerance=±5% power=0.25 resistance=220 package=THT]
  R2 = Resistor [tolerance=±5% power=0.25 resistance=220 package=THT]
  esp1 = ESP32 DevKitc V4
  Part1 = LCD1602-I2C

nets:
  N1: S1.Pin_1, S1.Pin_2, S2.Pin_1, S2.Pin_2, S3.Pin_1, S3.Pin_2, R1.Pin_0, esp1.GND#32
  N2: S1.Pin_3, S1.Pin_4, esp1.IO4
  N3: S2.Pin_3, S2.Pin_4, esp1.IO15
  N4: S3.Pin_3, S3.Pin_4, esp1.IO19
  N5: LED1.cathode, R2.Pin_1, esp1.IO12
  N6: LED2.cathode, R1.Pin_1
  N7: LED2.anode, esp1.IO32
  N8: esp1.IO21, Part1.SDA
  N9: esp1.IO22, Part1.SCL
  N10: esp1.GND#18, Part1.GND
  5V: esp1.5V, Part1.VCC

custom parts:
  ESP32 DevKitc V4: ESP32-DevKitC board with ESP32-WROOM-32 module. ESP32-DevKitC V4 is a small-sized ESP32-based development board produced by Espressif. Most of the pins on the ESP module are broken out to the pin headers on the board. The pins D0, D1, D2, D3, CMD and CLK are used internally for communication between ESP32 and SPI flash memory. They are grouped on both sides near the USB connector. Avoid using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
  LCD1602-I2C: A standard character display, usually with 2x16 characters. Comes in many colors with LCM1602 IIC attached.
